# Fritzing sketch 74HC595 (saved by Fritzing 0.9.3b)
breadboards: 1

parts:
  Part1 = Arduino Uno (Rev3)
  U2 = 74HC595 [package="DIP16 [THT]"]
  LED2 = 7-SEGMENT-4DIGIT-YOUNGSUN [package=7-segment-4digit-youngsun-longpads]  # not connected
  R8 = Resistor [tolerance=±5% resistance=220 package=THT]
  R9 = Resistor [tolerance=±5% resistance=220 package=THT]
  R10 = Resistor [tolerance=±5% resistance=220 package=THT]
  R11 = Resistor [tolerance=±5% resistance=220 package=THT]
  R12 = Resistor [tolerance=±5% resistance=220 package=THT]
  R13 = Resistor [tolerance=±5% resistance=220 package=THT]
  R14 = Resistor [tolerance=±5% resistance=220 package=THT]
  R15 = Resistor [tolerance=±5% resistance=220 package=THT]

nets:
  GND: Part1.GND, U2.GND, U2.OE
  N1: Part1.D2, U2.ST_CP
  N2: Part1.D3_PWM, U2.SH_CP
  N3: Part1.D4, U2.DS
  5V: Part1.5V, U2.MR, U2.VCC
  N4: U2.Q1, R13.Pin_0
  N5: U2.Q2, R11.Pin_1
  N6: U2.Q3, R9.Pin_1
  N7: U2.Q4, R8.Pin_1
  N8: U2.Q5, R14.Pin_0
  N9: U2.Q6, R12.Pin_1
  N10: U2.Q7, R10.Pin_1
  N11: U2.Q0, R15.Pin_0

custom parts:
  7-SEGMENT-4DIGIT-YOUNGSUN: This is a part for the 4-Digit 7-segment LEDs from Young Sun. Different from the Digikey LEDs, all 16 pins are used. The LONGPADS Variant is used for a test jig, but you may like it because there is more pad to solder to. If you are concerned about routing space, the standard works just fine though.
